# Fritzing sketch Ultrasonic sensor_ping_lib (saved by Fritzing 0.9.3b)
circuit board: 8.46667cm x 5.64444cm
breadboards: 1

parts:
  Part1 = Arduino Uno (Rev3)
  hc-sr1 = hc-sr04

nets (from the breadboard view):
  N1: Part1.D9_PWM, hc-sr1.Trig
  N2: Part1.D10_PWM/SS, hc-sr1.Echo
  GND: Part1.GND, hc-sr1.GND
  5V: Part1.5V, hc-sr1.VCC
