# Fritzing sketch Ultrasonic sensor (saved by Fritzing 0.9.3b)
circuit board: 8.46667cm x 5.64444cm
breadboards: 1

parts:
  Part1 = Arduino Uno (Rev3)
  hc-sr1 = hc-sr04

nets:
  GND: Part1.GND, hc-sr1.GND
  N1: Part1.D2, hc-sr1.Echo
  N2: Part1.D3_PWM, hc-sr1.Trig
  5V: Part1.5V, hc-sr1.VCC
