# Fritzing sketch Infrared_led (saved by Fritzing 0.9.3b)
circuit board: 8.46667cm x 5.64444cm
breadboards: 2

parts:
  IR1 = hx1838 [package=THT]
  Part1 = Arduino Uno (Rev3)
  LED1 = smd LED [color="Red (633nm)" package="0603 [SMD]"]

nets:
  GND: IR1.GND, Part1.GND, LED1.cathode
  N1: IR1.Sig, Part1.D7
  N2: Part1.D8, LED1.anode
