# Fritzing sketch Infrared_remote (saved by Fritzing 0.9.3b)
circuit board: 8.46667cm x 5.64444cm
breadboards: 1

parts:
  IR1 = hx1838 [package=THT]
  Part1 = Arduino Uno (Rev3)

nets:
  GND: IR1.GND, Part1.GND
  N1: IR1.Sig, Part1.D7
