# Fritzing sketch 74hc595 (saved by Fritzing 0.9.3b)
breadboards: 1

parts:
  U1 = 74HC595 [package="DIP16 [THT]"]
  Part1 = Arduino Uno (Rev3)

nets:
  GND: U1.GND, Part1.GND
  N1: U1.SH_CP, Part1.D6_PWM
  N2: U1.ST_CP, Part1.D5_PWM
  N3: U1.DS, Part1.D4
  VCC: U1.VCC, Part1.5V
