# Fritzing sketch keypad (saved by Fritzing 0.9.3b)

parts:
  Matrix_keypad1 = KEYPAD 4x4
  Part1 = Arduino Uno (Rev3)

nets:
  N1: Matrix_keypad1.col1, Part1.D2
  N2: Matrix_keypad1.col2, Part1.D3_PWM
  N3: Matrix_keypad1.col4, Part1.D5_PWM
  N4: Matrix_keypad1.row1, Part1.D6_PWM
  N5: Matrix_keypad1.row2, Part1.D7
  N6: Matrix_keypad1.row3, Part1.D8
  N7: Matrix_keypad1.row4, Part1.D9_PWM

custom parts:
  KEYPAD 4x4: Matrix keypad 16 buttons, 4 rows x 4 columns
