# Fritzing sketch 17DHT11 (saved by Fritzing 0.9.3b)
breadboards: 1

parts:
  DHT1 = DHT11 Humitidy and Temperature Sensor
  R1 = Resistor [tolerance=±5% resistance=10k package="0603 [SMD]"]
  Part1 = Arduino Uno (Rev3)

nets:
  VDD: DHT1.VDD, R1.Pin_0, Part1.5V
  N1: DHT1.DATA, R1.Pin_1, Part1.D8
  GND: DHT1.GND, Part1.GND

custom parts:
  DHT11 Humitidy and Temperature Sensor: DHT11 Humidity and Temperature Sensor
