# Fritzing sketch Air quality sensor_getting_ppm (saved by Fritzing 0.9.3b)

parts:
  Part1 = MQ-3 breakout
  Part2 = Arduino Uno (Rev3)

nets:
  VCC: Part1.VCC, Part2.5V
  GND: Part1.GND, Part2.GND
  N1: Part1.AO, Part2.A2

custom parts:
  MQ-3 breakout: Alcohol sensor is capable of detecting alcohol (ethanol) particles on itself and gives the information in digital form back to us to manipulate with it. SKU:101251 • Voltage: 5V DC • Power: max 750mW • Measurement range: 0.04-4mg/L
