# Fritzing sketch Sd-card module (saved by Fritzing 0.9.3b)
breadboards: 1

parts:
  microSD1 = MicroSD Card Module  # not connected
  microSD2 = MicroSD Card Module
  Part1 = Arduino Uno (Rev3)

nets:
  GND: microSD2.GND, Part1.GND
  VCC: microSD2.VCC, Part1.5V
  N1: microSD2.MISO, Part1.D12/MISO
  N2: microSD2.MOSI, Part1.D11_PWM/MOSI
  N3: microSD2.SCK, Part1.D13/SCK
  N4: microSD2.CS, Part1.D4
