# Fritzing sketch external eeprom (saved by Fritzing 0.9.3b)
breadboards: 1

parts:
  IC1 = 24LC256 [package=THT]
  Part1 = Arduino Uno (Rev3)

nets:
  N1: IC1.A0, IC1.A1, IC1.A2, IC1.0V, IC1.WP_-_Write_Protect, Part1.GND
  N2: IC1.SDA_-_I2C_Data, Part1.A4/SDA
  N3: IC1.SCL_-_I2C_Clock, Part1.A5/SCL
  N4: IC1.+V, Part1.5V
