# Fritzing sketch Stepper_motor (saved by Fritzing 0.9.3b)
breadboards: 1

parts:
  IC1 = L293D [package=THT]
  Part2 = Arduino Uno (Rev3)
  M1 = Stepper Motor - Bipolar

nets:
  N1: IC1.Enable_1, IC1.+Vmotor, IC1.Enable_2, IC1.+V, Part2.5V
  N2: IC1.In_1, Part2.D8
  N3: IC1.Out_1_(_Controlled_by_Enable_1_), M1.A
  N4: IC1.0V, Part2.GND
  N5: IC1.Out_2_(_Controlled_by_Enable_1_), M1.C
  N6: IC1.In_2, Part2.D9_PWM
  N7: IC1.In_3, Part2.D10_PWM/SS
  N8: IC1.Out_3_(_Controlled_by_Enable_2_), M1.B
  N9: IC1.Out_4_(_Controlled_by_Enable_2_), M1.D
  N10: IC1.In_4, Part2.D11_PWM/MOSI
