# Fritzing sketch circuit_sketch (saved by Fritzing 0.9.5d)
breadboards: 1

parts:
  Part1 = Arduino Uno (Rev3)
  R1 = Resistor [tolerance=±5% resistance=220 package=THT]
  LED1 = LED - 5mm [color="White (4500K)" package="5 mm [THT]"]

nets:
  N1: Part1.D8, R1.Pin_1
  N2: Part1.GND, LED1.cathode
  N3: R1.Pin_0, LED1.anode

notes:
  The long leg of the led is the anode (positive side) and the shorter leg is the cathode (negative side).
  Connect the anode to resistor then to the digital pin 8 and the cathode to ground

// code stored in the sketch: 1turningon.ino
int ledPin = 8;

void setup(){
    // initialize the digital pin as output
  pinMode(ledPin, OUTPUT);     
}

void loop() {
  digitalWrite(ledPin, HIGH);   // turn the ledPin on (HIGH is the voltage level)
}
