# Fritzing sketch circuit_sketch (saved by Fritzing 0.9.5d)
breadboards: 1

parts:
  Part2 = Arduino Uno (Rev3)
  LED4 = LED - 5mm [color="Red (633nm)" package="5 mm [THT]"]
  LED6 = LED - 5mm [color="Orange (605nm)" package="5 mm [THT]"]
  R4 = Resistor [tolerance=±5% resistance=220 package=THT]
  R5 = Resistor [tolerance=±5% resistance=220 package=THT]

nets:
  N1: Part2.D8, R4.Pin_1
  N2: Part2.D9_PWM, R5.Pin_1
  N3: Part2.GND, LED4.cathode, LED6.cathode
  N4: LED4.anode, R4.Pin_0
  N5: LED6.anode, R5.Pin_0

// code stored in the sketch: 4forloopblinking.ino
// This turns on the onboard LED for 1s and off for 0.5s repeatedly

int redLedPin = 8;
int yellowLedPin = 9;
int redWaitTimeOn = 300;
int redWaitTimeOff = 400;
int yellowWaitTimeOn = 250;
int yellowWaitTimeOff = 300;
int redNumBlink = 5;
int yellowNumBlink = 3;
int i,j ;

void setup(){
    // initialize the digital pin as output
  pinMode(redLedPin, OUTPUT);     
  pinMode(yellowLedPin, OUTPUT);
}

void loop() {
    for(i = 0 ; i <= redNumBlink ; i++ ){
        digitalWrite(redLedPin, HIGH);   // turn the LED on (HIGH is the voltage level)
        delay(redWaitTimeOn);               // wait for a 1 second
        digitalWrite(redLedPin, LOW);    // turn the LED off by making the voltage LOW
        delay(redWaitTimeOff); 
    }
    for(j = 0 ; j <= yellowNumBlink ; j++ ){
        digitalWrite(yellowLedPin, HIGH);   // turn the LED on (HIGH is the voltage level)
        delay(yellowWaitTimeOn);               // wait for a 1 second
        digitalWrite(yellowLedPin, LOW);    // turn the LED off by making the voltage LOW
        delay(yellowWaitTimeOff); 
    }
}
