# Fritzing sketch circuit_sketch (saved by Fritzing 0.9.5d)
breadboards: 1

parts:
  Part3 = Arduino Uno (Rev3)
  R6 = Resistor [tolerance=±5% resistance=220 package=THT]
  LED7 = LED - 5mm [color="Orange (605nm)" package="5 mm [THT]"]
  LED8 = LED - 5mm [color="Red (633nm)" package="5 mm [THT]"]
  R7 = Resistor [tolerance=±5% resistance=220 package=THT]

nets:
  N1: Part3.D8, R6.Pin_1
  N2: Part3.D9_PWM, R7.Pin_1
  N3: Part3.GND, LED7.cathode, LED8.cathode
  N4: R6.Pin_0, LED8.anode
  N5: LED7.anode, R7.Pin_0

// code stored in the sketch: 4loopblinking.ino
// This turns on the onboard LED for 1s and off for 0.5s repeatedly

int redLedPin = 8;
int yellowLedPin = 9;
int redWaitTimeOn = 300;
int redWaitTimeOff = 200;
int yellowWaitTimeOn = 250;
int yellowWaitTimeOff = 300;
int redNumBlink = 5;
int yellowNumBlink = 8;
int i,j ;

void setup(){
    // initialize the digital pin as output
  pinMode(redLedPin, OUTPUT);     
  pinMode(yellowLedPin, OUTPUT);
}

void loop() {
    for(i = 0 ; i <= redNumBlink ; i++ ){
        digitalWrite(redLedPin, HIGH);   // turn the LED on (HIGH is the voltage level)
        delay(redWaitTimeOn);               // wait for a 1 second
        digitalWrite(redLedPin, LOW);    // turn the LED off by making the voltage LOW
        delay(redWaitTimeOff); 
    }
    j = 0;
    while(j <= yellowNumBlink){
        digitalWrite(yellowLedPin, HIGH);   // turn the LED on (HIGH is the voltage level)
        delay(yellowWaitTimeOn);               // wait for a 1 second
        digitalWrite(yellowLedPin, LOW);    // turn the LED off by making the voltage LOW
        delay(yellowWaitTimeOff); 
        j += 1;
    }
}
