# Fritzing sketch circuit_sketch (saved by Fritzing 0.9.5d)
breadboards: 1

parts:
  Part4 = Arduino Uno (Rev3)
  R8 = Resistor [tolerance=±5% resistance=220 package=THT]
  LED9 = LED - 5mm [color="Orange (605nm)" package="5 mm [THT]"]
  LED10 = LED - 5mm [color="Red (633nm)" package="5 mm [THT]"]
  R9 = Resistor [tolerance=±5% resistance=220 package=THT]

nets:
  N1: Part4.D8, R8.Pin_1
  N2: Part4.D9_PWM, R9.Pin_1
  N3: Part4.GND, LED9.cathode, LED10.cathode
  N4: R8.Pin_0, LED10.anode
  N5: LED9.anode, R9.Pin_0

// code stored in the sketch: 6getting_data_from_serial_blinking_led.ino
// This turns on the onboard LED for 1s and off for 0.5s repeatedly

int redLedPin = 8;
int yellowLedPin = 9;
int redWaitTimeOn = 400;
int redWaitTimeOff = 300;
int yellowWaitTimeOn = 200;
int yellowWaitTimeOff = 200;
int redNumBlink;
int yellowNumBlink;
int i,j;
String redMessage = "\n\nThe Red LED is blinking";
String yellowMessage = "\nThe Yellow LED is blinking\n";
String blinkMessage = "\tYou are on blink : ";


void setup(){
    // initialize the digital pin as output
  pinMode(redLedPin, OUTPUT);     
  pinMode(yellowLedPin, OUTPUT);
  Serial.begin(115200);

  Serial.println("How many times do you want the RED led to blink: ");
  while(Serial.available() == 0){  }
  redNumBlink = Serial.parseInt();

  Serial.println("How many times do you want the YELLOW led to blink: ");
  while(Serial.available() == 0){  }
  yellowNumBlink = Serial.parseInt();
}

void loop() {
    Serial.println(redMessage);
    for(i = 0 ; i <= redNumBlink ; i++){
        Serial.print(blinkMessage);
        Serial.println(i);
        digitalWrite(redLedPin, HIGH);   // turn the LED on (HIGH is the voltage level)
        delay(redWaitTimeOn);               // wait for a 1 second
        digitalWrite(redLedPin, LOW);    // turn the LED off by making the voltage LOW
        delay(redWaitTimeOff); 
    }
    Serial.print(yellowMessage + blinkMessage);
    for(j = 0 ; j <= yellowNumBlink ; j++){
        Serial.print(j);
        digitalWrite(yellowLedPin, HIGH);   // turn the LED on (HIGH is the voltage level)
        delay(yellowWaitTimeOn);               // wait for a 1 second
        digitalWrite(yellowLedPin, LOW);    // turn the LED off by making the voltage LOW
        delay(yellowWaitTimeOff); 
    }
}
