# Fritzing sketch circuit_sktech (saved by Fritzing 0.9.5d)
breadboards: 1

parts:
  Part4 = Arduino Uno (Rev3)
  R8 = Resistor [tolerance=±5% resistance=220 package=THT]
  LED9 = LED - 5mm [color="White (8000K)" package="5 mm [THT]"]
  LED10 = LED - 5mm [color="Blue (430nm)" package="5 mm [THT]"]
  R9 = Resistor [tolerance=±5% resistance=220 package=THT]

nets:
  N1: Part4.D8, R8.Pin_1
  N2: Part4.D9_PWM, R9.Pin_1
  N3: Part4.GND, LED9.cathode, LED10.cathode
  N4: R8.Pin_0, LED10.anode
  N5: LED9.anode, R9.Pin_0

// code stored in the sketch: 7analog_writing_voltages_gradually_light_led.ino
// This turns on the onboard LED for 1s and off for 0.5s repeatedly

int whiteLedPin = 9;
int whiteWaitTimeOn = 5;
int whiteWaitTimeOff = 10;
int whiteNumBlink = 2;
int blueLedPin = 10;
int blueWaitTimeOn = 5;
int blueWaitTimeOff = 10;
int blueNumBlink = 1;
int i,j ;

void setup(){
    // initialize the digital pin as output
  pinMode(whiteLedPin, OUTPUT);     
    pinMode(blueLedPin, OUTPUT);     

}

void loop() {
  for (i = 0; i <= whiteNumBlink; i++){
    for(j = 0 ; j <= 255 ; j++ ){
        analogWrite(whiteLedPin, j);   // turn the LED on (HIGH is the voltage level)
        delay(whiteWaitTimeOn);               // wait for a 1 second
    }
    analogWrite(whiteLedPin, 0);    // turn the LED off by making the voltage LOW
    delay(whiteWaitTimeOff); 
   }
  for (i = 0; i <= blueNumBlink; i++){
    for(j = 0 ; j <= 255 ; j++ ){
        analogWrite(blueLedPin, j);   // turn the LED on (HIGH is the voltage level)
        delay(blueWaitTimeOn);               // wait for a 1 second
    }
    analogWrite(blueLedPin, 0);    // turn the LED off by making the voltage LOW
    delay(blueWaitTimeOff); 
   }

}
