# Fritzing sketch circuit_sketch (saved by Fritzing 0.9.5d)
breadboards: 1

parts:
  Part4 = Arduino Uno (Rev3)
  LED10 = LED - 5mm [color="Yellow (592nm)" package="5 mm [THT]"]
  R9 = Resistor [tolerance=±5% resistance=220 package=THT]
  LED9 = LED - 5mm [color="Red (633nm)" package="5 mm [THT]"]
  LED11 = LED - 5mm [color="Green (560nm)" package="5 mm [THT]"]
  LED12 = LED - 5mm [color="Green (565nm)" package="5 mm [THT]"]
  LED13 = LED - 5mm [color="Yellow (592nm)" package="5 mm [THT]"]
  LED14 = LED - 5mm [color="Blue (470nm)" package="5 mm [THT]"]
  LED15 = LED - 5mm [color="Blue (470nm)" package="5 mm [THT]"]
  LED16 = LED - 5mm [color="White (6500K)" package="5 mm [THT]"]
  LED17 = LED - 5mm [color="White (6500K)" package="5 mm [THT]"]
  LED18 = LED - 5mm [color="Red (633nm)" package="5 mm [THT]"]
  R10 = Resistor [tolerance=±5% resistance=220 package=THT]
  R11 = Resistor [tolerance=±5% resistance=220 package=THT]
  R12 = Resistor [tolerance=±5% resistance=220 package=THT]
  R13 = Resistor [tolerance=±5% resistance=220 package=THT]
  R14 = Resistor [tolerance=±5% resistance=220 package=THT]
  R15 = Resistor [tolerance=±5% resistance=220 package=THT]
  R16 = Resistor [tolerance=±5% resistance=220 package=THT]
  R17 = Resistor [tolerance=±5% resistance=220 package=THT]
  R18 = Resistor [tolerance=±5% resistance=220 package=THT]

nets:
  N1: Part4.D8, R13.Pin_1
  N2: Part4.D9_PWM, R15.Pin_1
  N3: Part4.D10_PWM/SS, R12.Pin_1
  N4: Part4.D11_PWM/MOSI, R11.Pin_1
  N5: Part4.D12/MISO, R10.Pin_1
  N6: Part4.D13/SCK, R9.Pin_1
  N7: Part4.GND, LED10.cathode, LED9.cathode, LED11.cathode, LED12.cathode, LED13.cathode, LED15.cathode, LED16.cathode, LED17.cathode, LED18.cathode
  N8: Part4.D4, R18.Pin_1
  N9: Part4.D5_PWM, R17.Pin_1
  N10: Part4.D6_PWM, R16.Pin_1
  N11: Part4.D7, R14.Pin_1
  N12: LED10.anode, R12.Pin_0
  N13: R9.Pin_0, LED18.anode
  N14: LED9.anode, R10.Pin_0
  N15: LED11.anode, R13.Pin_0
  N16: LED12.anode, R15.Pin_0
  N17: LED13.anode, R11.Pin_0
  N18: LED14.anode, R16.Pin_0
  N19: LED15.anode, R14.Pin_0
  N20: LED16.anode, R18.Pin_0
  N21: LED17.anode, R17.Pin_0

// code stored in the sketch: 8flowing_led.ino
int lowestPin = 4;
int highestPin = 13;
int delayTime = 250;

void setup(){
    for(int pin = lowestPin; pin <= highestPin; pin++){
        pinMode(pin, OUTPUT);
    }
}

void loop(){
    for(int pin = lowestPin; pin <= highestPin; pin++){
        digitalWrite(pin, HIGH);
        delay(delayTime);
    }
    for(int pin = highestPin; pin >= lowestPin; pin--){
        digitalWrite(pin, LOW);
        delay(delayTime);
    }
    for(int pin = highestPin; pin >= lowestPin; pin--){
        digitalWrite(pin, HIGH);
        delay(delayTime);
    }
    for(int pin = lowestPin; pin <= highestPin; pin++){
        digitalWrite(pin, LOW);
        delay(delayTime);
    }

}
