# Fritzing sketch potentiometer-dimming-led (saved by Fritzing 0.9.3b)
breadboards: 1

parts:
  U1 = POT [package=pot_mammoth]
  Part1 = Arduino Uno (Rev3)
  LED2 = smd LED [color="Red (633nm)" package="0603 [SMD]"]

nets:
  N1: U1.S, Part1.GND
  N2: U1.A, Part1.A0
  N3: U1.E, Part1.5V
  N4: Part1.D9_PWM, LED2.anode
